# Fritzing sketch architecture_robocar (saved by Fritzing 0.9.3b)

parts:
  Raspberry_Pi_1 = Raspberry Pi 3 [part_number=RPI-3-V1.2]  # not connected
  Part1 = 16-Channel 12-bit PWM Servo Driver - I2C [part_number=815]
  J1 = Basic Servo
  J2 = Basic Servo
  Part2 = Arduino Nano (Rev3.0)
  JP4 = Header 3 [package=screwterminal-3.5mm-3_lock.007s]
  JP5 = Header 3 [package=screwterminal-3.5mm-3_lock.007s]

nets:
  VCC: Part1.5.0V, Part1.VCC, J1.vcc, J2.vcc, Part2.D9, JP4.2
  GND: Part1.GND, J1.gnd, J2.gnd, Part2.GND, JP4.3
  N1: Part1.PWM1, J2.pulse
  N2: Part1.PWM0, J1.pulse
  N3: Part1.SDA, Part2.A4
  N4: Part1.SCL, Part2.A5
  N5: Part2.D10, JP4.1
  N6: Part2.D11/MOSI, JP5.1

notes:
  The second servo is actually ESC+Motor, but the controls are the same
  Arduino serves as a multiplexer for RC controls and Raspberry controls
  Power wire from ESC (red) supplies PCA9685 and RC receiver
  ESC
  PCA9685
  1
  2
  Channel 2
  Channel 1
  RC Radio Receiver
  3
  4
  5
  6
  7
  8
  9
  Standard Donkeycar architecture
  Robocar architecture
  PCA9685 by https://github.com/adafruit/Fritzing-Library

custom parts:
  16-Channel 12-bit PWM Servo Driver - I2C: You want to make a cool robot, maybe a hexapod walker, or maybe just a piece of art with a lot of moving parts. Or maybe you want to drive a lot of LEDs with precise PWM output. Using only two pins, control 16 free-running PWM outputs! You can even chain up 62 breakouts to control up to 992 PWM outputs.
