# Fritzing sketch sketch (saved by Fritzing 0.9.3b)
breadboards: 1

parts:
  Part1 = Arduino Nano (Rev3.0)
  LED0 = LED - 3mm [color="Blue (505nm)" package="3 mm [THT]"]
  Part2 = Adafruit PCA9685 PWM/Servo Breakout [part_number=815]
  LED1 = LED - 3mm [color="Red (633nm)" package="3 mm [THT]"]
  R1 = Resistor [tolerance=±5% resistance=330 package="0402 [SMD]"]
  R2 = Resistor [tolerance=±5% resistance=330 package="0402 [SMD]"]

nets:
  GND: Part1.GND, Part2.GND, R1.Pin_0, R2.Pin_0
  5V: Part1.5V, Part2.VCC
  N1: Part1.A5, Part2.SCL
  N2: Part1.A4, Part2.SDA
  N3: LED0.cathode, R1.Pin_1
  N4: LED0.anode, Part2.PWM0
  N5: Part2.PWM1, LED1.anode
  N6: LED1.cathode, R2.Pin_1

notes:
  PCA9685 by https://github.com/adafruit/Fritzing-Library

custom parts:
  Adafruit PCA9685 PWM/Servo Breakout: Using only two pins, control 16 free-running PWM outputs! I2C-controlled PWM driver with a built in clock. Unlike the TLC5940 family, you do not need to continuously send it signal tying up your microcontroller, its completely free running! 5V compliant, which means you can control it from a 3.3V microcontroller and still safely drive up to 6V outputs (this is good for when you want to control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
